# Fritzing sketch gy_color_sensor_tsc230 (saved by Fritzing 0.9.2b)
breadboards: 1

parts:
  Eleman1 = Arduino Nano (Rev3.0)
  Servo_a = Basic Servo
  Servo_b = Basic Servo

nets:
  N1: Eleman1.D9, Servo_a.pulse
  N2: Eleman1.D10, Servo_b.pulse
  GND: Servo_a.gnd, Servo_b.gnd
  VCC: Servo_a.vcc, Servo_b.vcc
